// Digital circuit 6502_basic.dig as structural Verilog
module _6502_basic (
  input  clk
);

  wire _6502_wr, and_1_out, and_2_out, and_3_out, RST_out;
  wire [7:0] _6502_da;
  wire [15:0] _6502_ad;

  Button RST (.out(RST_out));
  cpu_6502 _6502 (.RST(RST_out), .NMI(1'b0), .INT(1'b0), .CLK(clk), .AD(_6502_ad), .DA(_6502_da), .WR(_6502_wr));
  and and_1 (and_1_out, ~_6502_ad[14], _6502_ad[15]);  // And
  and and_2 (and_2_out, and_1_out, _6502_wr);
  and and_3 (and_3_out, and_1_out, ~_6502_wr);  // And
  RAMSinglePortSel #(.AddrBits(15), .Bits(8)) RAM_32K (
    .A(_6502_ad[14:0]), .CS(~_6502_ad[15]), .WE(_6502_wr), .OE(~_6502_wr), .D(_6502_da));
  RAMSinglePortSel #(.AddrBits(14), .isProgramMemory("true"), .Bits(8)) BASIC_ROM_16K (
    .A(_6502_ad[13:0]), .CS(_6502_ad[14]), .WE(1'b0), .OE(_6502_ad[15]), .D(_6502_da));
  Telnet #(.telnetEscape("false")) telnet_1 (
    .in(_6502_da), .C(clk), .wr(and_2_out), .rd(and_3_out), .out(_6502_da));  // open: av

  // Notes on the sheet:
  //   clk: Hz: 2147483647
endmodule
