// Digital circuit 6502test.dig as structural Verilog
module _6502test (
  input  clk
);

  wire Address_Decoder_eq, Address_Decoder_gt, OE_RAM, OE_TER, WR, WR_RAM, WR_TER;
  wire [7:0] D;
  wire [15:0] A;
  wire [15:8] Input_d;

  cpu #(.generic("cpuModel := 0;")) _6502 (
    .RST(1'b0), .NMI(1'b0), .INT(1'b0), .CLK(clk), .AD(A), .DA(D), .WR(WR));  // open: OE
  RAMSinglePort #(.AddrBits(16), .isProgramMemory("true"), .Bits(8)) RAM (
    .A(A), .str(WR_RAM), .C(clk), .ld(OE_RAM), .D(D));
  Terminal Output (.D(D), .C(clk), .en(WR_TER));
  Keyboard Input (.C(clk), .en(OE_TER), .D({Input_d, D}));  // open: av
  Comparator #(.Bits(16)) Address_Decoder (
    .a(A), .b({16{1'b0}}), .gt(Address_Decoder_gt), .eq(Address_Decoder_eq));  // open: lt
  and and_1 (OE_RAM, Address_Decoder_gt, ~WR);  // And
  and and_2 (WR_RAM, Address_Decoder_gt, WR);
  and and_3 (OE_TER, Address_Decoder_eq, ~WR);  // And
  and and_4 (WR_TER, Address_Decoder_eq, WR);

  // Notes on the sheet:
  //   clk: Hz: 2147483647
endmodule
