// Digital circuit alu.dig as structural Verilog
module alu (
  input  [7:0] A,
  input  [7:0] B,
  input  C_i,
  input  D_i,
  input  [3:0] Op,
  input  OE,
  output [7:0] BUS,
  output [7:0] Y,
  output C_o,
  output V
);

  wire and_4_out, and_5_out, C_D, C_HI, C_LO, HI_2_c_o, LO_2_c_do;
  wire [3:0] B_HI, B_LO, HI_2_d_o, LO_2_d_o, Y_HI, Y_LO;
  wire [7:0] B_DEC, not_1_out, Y_AINV, Y_AND, Y_CLRB, Y_DSUM, Y_OR, Y_SETB, Y_TSTB, Y_XOR;

  assign not_1_out = ~B;  // Not not_1, 8 bits wide
  Multiplexer #(.Bits(8)) multiplexer_1 (.sel(Op[0]), .in_0(B), .in_1(not_1_out), .out({B_HI, B_LO}));
  Decoder #(.Selector_Bits(3)) decoder_1 (
    .sel(B[2:0]), .out_0(B_DEC[0]), .out_1(B_DEC[1]), .out_2(B_DEC[2]), .out_3(B_DEC[3]), .out_4(B_DEC[4]),
    .out_5(B_DEC[5]), .out_6(B_DEC[6]), .out_7(B_DEC[7]));
  Multiplexer #(.Selector_Bits(4), .Bits(8)) multiplexer_2 (
    .sel(Op), .in_0({Y_HI, Y_LO}), .in_1({Y_HI, Y_LO}), .in_2(Y_DSUM), .in_3(Y_DSUM), .in_4(Y_AND),
    .in_5(Y_OR), .in_6(Y_XOR), .in_7({C_i, A[7:1]}), .in_8(Y_CLRB), .in_9(Y_SETB), .in_10(Y_TSTB),
    .in_11(Y_AINV), .in_12({8{1'b0}}), .in_13({8{1'b0}}), .in_14({8{1'b0}}), .in_15({8{1'b0}}), .out(Y));
  Add #(.Bits(4)) LO (.a(A[3:0]), .b(B_LO), .c_i(C_i), .s(Y_LO), .c_o(C_LO));
  bcd LO_2 (.S_i(Y_LO), .C_i(C_LO), .C_di(1'b0), .SUB(Op[0]), .D_o(LO_2_d_o), .C_do(LO_2_c_do));  // open: C_o
  assign Y_AND = A & B;  // And and_1, 8 bits wide
  assign Y_XOR = A ^ B;  // XOr xor_1, 8 bits wide
  assign Y_CLRB = A & ~B_DEC;  // And and_2, 8 bits wide
  assign Y_TSTB = A & B_DEC;  // And and_3, 8 bits wide
  assign BUS = OE ? Y : 8'bz;  // Driver driver_1
  Add #(.Bits(4)) HI (.a(A[7:4]), .b(B_HI), .c_i(C_LO), .s(Y_HI), .c_o(C_HI));
  bcd HI_2 (.S_i(Y_HI), .C_i(C_HI), .C_di(LO_2_c_do), .SUB(Op[0]), .D_o(HI_2_d_o), .C_o(HI_2_c_o));  // open: C_do
  assign Y_OR = A | B;  // Or or_1, 8 bits wide
  assign Y_SETB = A | B_DEC;  // Or or_2, 8 bits wide
  assign Y_AINV = ~A;  // Not not_2, 8 bits wide
  Multiplexer #(.Selector_Bits(4)) multiplexer_3 (
    .sel(Op), .in_0(C_HI), .in_1(C_HI), .in_2(C_D), .in_3(C_D), .in_4(1'b0), .in_5(1'b0), .in_6(1'b0),
    .in_7(A[0]), .in_8(1'b0), .in_9(1'b0), .in_10(1'b0), .in_11(1'b0), .in_12(1'b0), .in_13(1'b0),
    .in_14(1'b0), .in_15(1'b0), .out(C_o));
  Multiplexer #(.Bits(8)) multiplexer_4 (.sel(D_i), .in_0({Y_HI, Y_LO}), .in_1({HI_2_d_o, LO_2_d_o}), .out(Y_DSUM));
  Multiplexer multiplexer_5 (.sel(D_i), .in_0(C_HI), .in_1(HI_2_c_o), .out(C_D));
  and and_4 (and_4_out, ~A[7], ~B_HI[3], Y_HI[3]);  // And
  and and_5 (and_5_out, A[7], B_HI[3], ~Y_HI[3]);  // And
  or or_3 (V, and_4_out, and_5_out);

  // Other names for the same wires on the sheet: B_SI = B_HI[3]; A_LO[3:0] = A[3:0]; C_SHR = A[0];
  //   Y_SHR[7:0] = {C_i, A[7:1]}; A_HI[3:0] = A[7:4]; A_SI = A[7]; SUB = Op[0]; Y_SUM[7:0] = {Y_HI, Y_LO};
  //   Y_SI = Y_HI[3]
endmodule

/* Test case Add / Sub:
Op D_i A B C_i C_o Y V

loop(ci, 2) loop(a, 256) loop(b, 256)
 # Binary Add
  let y = a + b + ci;
  let co = (y >> 8 & 1);
  let as = a >> 7; let bs = b >> 7; let ys = (y & 0x80) >> 7;
  let v = (!as & !bs & ys) | (as & bs & !ys);
  0 0 (a) (b) (ci) (co) (y) (v)
  0 1 (a) (b) (ci) (co) (y) (v)
  2 0 (a) (b) (ci) (co) (y) (v)

 # Binary Subtract
  let y = a - b - !ci;
  let co = !(y >> 8 & 1);
  let as = a >> 7; let bs = b >> 7; let ys = (y & 0x80) >> 7;
  let v = (!as & bs & ys) | (as & !bs & !ys);
  1 0 (a) (b) (ci) (co) (y) (v)
  1 1 (a) (b) (ci) (co) (y) (v)
  3 0 (a) (b) (ci) (co) (y) (v)
end loop end loop end loop
*/

/* Test case BCD Add / Sub:
# https://stackoverflow.com/questions/29875541/binary-coded-decimal-addition-using-integer
#
# /* Add two packed BCD operands, where each uint32_t holds 8 BCD digits * /
# uint32_t bcd_add (uint32_t x, uint32_t y)
# {
#     uint32_t t0, t1;
#     t0 = x + 0x66666666;         // force nibble carry when BCD digit > 9
#     t1 = x ^ y;                  // bit-wise sum
#     t0 = t0 + y;                 // addition with nibble carry
#     t1 = t1 ^ t0;                // (x ^ y) ^ (x + y)
#     t0 = t0 < y;                 // capture carry-out from bit 31
#     t1 = (t1 >> 1) | (t0 << 31); // nibble carry-outs in bits 3, 7, ..., 31
#     t0 = t1 & 0x88888888;        // extract nibble carry-outs 
#     t1 = t0 >> 2;                // 8 - (8 >> 2) = 6
#     return x + y + (t0 - t1);    // add 6 to any digit with nibble carry-out
# }
#
# /* Knuth, TAOCP Vol.4A Part 1 * /
# uint32_t median (uint32_t x, uint32_t y, uint32_t z)
# {
#      return (x & (y | z)) | (y & z);
# }
# 
# uint32_t bcd_add_knuth (uint32_t x, uint32_t y)
# {
#     uint32_t z, u, t;
#     z = y + 0x66666666;
#     u = x + z;
#     t = median (~x, ~z, u) & 0x88888888;
#     return u - t + (t >> 2);
# }

Op D_i A B C_i C_o Y

loop(ci, 2) loop(ah, 10) loop(al, 10) loop(bh, 10) loop(bl, 10)
  # --- BCD Add ---
  let a = (ah << 4) | (al);
  let b = (bh << 4) | (bl);

  # A + B = Y
  let z = b + 0x66;
  let u = a + z;
  let m = (~a & (~z | u)) | (~z & u);
  let t = m & 0x88;
  let y = u - t + (t >> 2);

  # Y + C = Y
  let z = ci + 0x66;
  let u = y + z;
  let m = (~y & (~z | u)) | (~z & u);
  let t = m & 0x88;
  let y = u - t + (t >> 2);

  let co = y >> 8;
  let y = y & 0xff;

  2 1 (a) (b) (ci) (co) (y)

  # --- BCD Subtract ---
  # 9's complement of b
  let bc = ((9 - bh) << 4) | (9 - bl);

  # A + /B = Y
  let z = bc + 0x66;
  let u = a + z;
  let m = (~a & (~z | u)) | (~z & u);
  let t = m & 0x88;
  let y = u - t + (t >> 2);

  # Y + C = Y
  let z = ci + 0x66;
  let u = y + z;
  let m = (~y & (~z | u)) | (~z & u);
  let t = m & 0x88;
  let y = u - t + (t >> 2);

  let co = y >> 8;
  let y = y & 0xff;

  3 1 (a) (b) (ci) (co) (y)
end loop end loop end loop end loop end loop
*/

/* Test case AND / OR / XOR:
Op A B Y

loop(a, 256) loop(b, 256)
  # AND
  let y = a & b;
  4 (a) (b) (y)

  # OR
  let y = a | b;
  5 (a) (b) (y)

  # XOR
  let y = a ^ b;
  6 (a) (b) (y)
end loop end loop
*/

/* Test case SHR:
Op A C_i C_o Y

# SHR
loop(ci, 2) loop(a, 256)
  let y = (ci << 7) | (a >> 1);
  let co = a & 1;
  7 (a) (ci) (co) (y)
end loop end loop
*/

/* Test case Bit Set / Clear / Test:
Op A B Y

loop(a, 256) loop(b, 8)
  # Decoded B
  let bd = 1 << b;

  # Clear Bit
  let y = a & ~bd;
  8 (a) (b) (y)

  # Set Bit
  let y = a | bd;
  9 (a) (b) (y)

  # Test Bit
  let y = a & bd;
  10 (a) (b) (y)
end loop end loop
*/
