// Digital circuit bcd.dig as structural Verilog
module bcd (
  input  [3:0] S_i,
  input  C_i,
  input  C_di,
  input  SUB,
  output [3:0] D_o,
  output C_o,
  output C_do
);

  wire and_1_out, comparator_1_eq, comparator_1_gt, or_1_out, or_2_out;
  wire [3:0] add_1_s, multiplexer_1_out, multiplexer_2_out, sub_1_s;

  Comparator #(.Bits(4)) comparator_1 (.a(S_i), .b(4'b1001), .gt(comparator_1_gt), .eq(comparator_1_eq));  // open: lt
  and and_1 (and_1_out, comparator_1_eq, C_di);
  or or_1 (or_1_out, comparator_1_gt, C_i, and_1_out);
  Multiplexer #(.Bits(4)) multiplexer_1 (.sel(or_1_out), .in_0(4'b0000), .in_1(4'b0110), .out(multiplexer_1_out));
  Multiplexer #(.Bits(4)) multiplexer_2 (.sel(C_i), .in_0(4'b0110), .in_1(4'b0000), .out(multiplexer_2_out));
  Add #(.Bits(4)) add_1 (.a(S_i), .b(multiplexer_1_out), .c_i(C_di), .s(add_1_s), .c_o(C_do));
  Sub #(.Bits(4)) sub_1 (.a(S_i), .b(multiplexer_2_out), .c_i(1'b0), .s(sub_1_s));  // open: c_o
  or or_2 (or_2_out, C_i, C_do);
  Multiplexer #(.Bits(4)) multiplexer_3 (.sel(SUB), .in_0(add_1_s), .in_1(sub_1_s), .out(D_o));
  Multiplexer multiplexer_4 (.sel(SUB), .in_0(or_2_out), .in_1(C_i), .out(C_o));
endmodule
