// Digital circuit address.dig as structural Verilog
module address (
  input  [7:0] PC_L,
  input  [7:0] PC_H,
  input  [7:0] AD_L,
  input  [7:0] AD_H,
  input  [7:0] SP,
  input  [1:0] SEL_AD,
  output [15:0] AD
);

  Multiplexer #(.Selector_Bits(2), .Bits(16)) multiplexer_1 (
    .sel(SEL_AD), .in_0({PC_H, PC_L}), .in_1({AD_H, AD_L}), .in_2({{8{1'b0}}, AD_L}), .in_3({8'h1, SP}),
    .out(AD));
endmodule
