// Digital circuit alu_6502_nobcd.dig as structural Verilog
module alu_6502_nobcd (
  input  [7:0] A,
  input  [7:0] B,
  input  C_i,
  input  D_i,
  input  [2:0] Op,
  input  OE,
  output [7:0] BUS,
  output [7:0] Y,
  output C_o,
  output V
);

  wire and_2_out, and_3_out, B_SI, C_o_t, Y_SI;
  wire [6:0] multiplexer_2_out, Y_SUM;
  wire [7:0] not_1_out, Y_AND, Y_OR, Y_XOR;

  assign Y_AND = A & B;  // And and_1, 8 bits wide
  assign Y_XOR = A ^ B;  // XOr xor_1, 8 bits wide
  assign not_1_out = ~B;  // Not not_1, 8 bits wide
  Multiplexer #(.Selector_Bits(3), .Bits(8)) multiplexer_1 (
    .sel(Op), .in_0({Y_SI, Y_SUM}), .in_1({Y_SI, Y_SUM}), .in_2({Y_SI, Y_SUM}), .in_3({Y_SI, Y_SUM}),
    .in_4(Y_AND), .in_5(Y_OR), .in_6(Y_XOR), .in_7({C_i, A[7:1]}), .out(Y));
  Multiplexer #(.Bits(8)) multiplexer_2 (.sel(Op[0]), .in_0(B), .in_1(not_1_out), .out({B_SI, multiplexer_2_out}));
  Add #(.Bits(8)) add_1 (.a(A), .b({B_SI, multiplexer_2_out}), .c_i(C_i), .s({Y_SI, Y_SUM}), .c_o(C_o_t));
  assign Y_OR = A | B;  // Or or_1, 8 bits wide
  assign BUS = OE ? Y : 8'bz;  // Driver driver_1
  and and_2 (and_2_out, ~A[7], ~B_SI, Y_SI);  // And
  and and_3 (and_3_out, A[7], B_SI, ~Y_SI);  // And
  Multiplexer #(.Selector_Bits(3)) multiplexer_3 (
    .sel(Op), .in_0(C_o_t), .in_1(C_o_t), .in_2(C_o_t), .in_3(C_o_t), .in_4(1'b0), .in_5(1'b0), .in_6(1'b0),
    .in_7(A[0]), .out(C_o));
  or or_2 (V, and_2_out, and_3_out);

  // Other names for the same wires on the sheet: C_SHR = A[0]; Y_SHR[7:0] = {C_i, A[7:1]}; A_SI = A[7]; SUB = Op[0];
  //   Y_SUM[7] = Y_SI
endmodule

/* Test case Add / Sub:
Op D_i A B C_i C_o Y V

loop(ci, 2) loop(a, 256) loop(b, 256)
 # Binary Add
  let y = a + b + ci;
  let co = (y >> 8 & 1);
  let as = a >> 7; let bs = b >> 7; let ys = (y & 0x80) >> 7;
  let v = (!as & !bs & ys) | (as & bs & !ys);
  0 0 (a) (b) (ci) (co) (y) (v)
  0 1 (a) (b) (ci) (co) (y) (v)
  2 0 (a) (b) (ci) (co) (y) (v)

 # Binary Subtract
  let y = a - b - !ci;
  let co = !(y >> 8 & 1);
  let as = a >> 7; let bs = b >> 7; let ys = (y & 0x80) >> 7;
  let v = (!as & bs & ys) | (as & !bs & !ys);
  1 0 (a) (b) (ci) (co) (y) (v)
  1 1 (a) (b) (ci) (co) (y) (v)
  3 0 (a) (b) (ci) (co) (y) (v)
end loop end loop end loop
*/

/* Test case AND / OR / XOR:
Op A B Y

loop(a, 256) loop(b, 256)
  # AND
  let y = a & b;
  4 (a) (b) (y)

  # OR
  let y = a | b;
  5 (a) (b) (y)

  # XOR
  let y = a ^ b;
  6 (a) (b) (y)
end loop end loop
*/

/* Test case SHR:
Op A C_i C_o Y

# SHR
loop(ci, 2) loop(a, 256)
  let y = (ci << 7) | (a >> 1);
  let co = a & 1;
  7 (a) (ci) (co) (y)
end loop end loop
*/
