// Digital circuit constant.dig as structural Verilog
module constant (
  input  [3:0] IN,
  input  OE,
  output [7:0] BUS,
  output [7:0] REG
);

  assign BUS = OE ? {{5{IN[3]}}, IN[2:0]} : 8'bz;  // Driver driver_1

  assign REG = {{5{IN[3]}}, IN[2:0]};
endmodule
