// Digital circuit counter.dig as structural Verilog
module counter (
  input  EN,
  input  DIR,
  input  WR,
  input  OE,
  input  CLK,
  output [7:0] BUS,
  output [7:0] REG,
  output OV
);

  CounterPreset #(.Bits(8)) counterpreset_1 (
    .en(EN), .C(CLK), .dir(DIR), .in(BUS), .ld(WR), .clr(1'b0), .out(REG), .ovf(OV));
  assign BUS = OE ? REG : 8'bz;  // Driver driver_1
endmodule
