// Digital circuit flags.dig as structural Verilog
module flags (
  input  WR,
  input  C_i,
  input  Z_i,
  input  B_i,
  input  V_i,
  input  N_i,
  input  U_C,
  input  U_Z,
  input  U_I,
  input  U_D,
  input  U_V,
  input  U_N,
  input  OE,
  input  CLK,
  output [7:0] BUS,
  output C_o,
  output Z_o,
  output I_o,
  output D_o,
  output V_o,
  output N_o,
  output [7:0] REG
);

  wire multiplexer_1_out, multiplexer_2_out, multiplexer_3_out, multiplexer_4_out;

  Multiplexer multiplexer_1 (.sel(WR), .in_0(C_i), .in_1(BUS[0]), .out(multiplexer_1_out));
  Multiplexer multiplexer_2 (.sel(WR), .in_0(V_i), .in_1(BUS[6]), .out(multiplexer_2_out));
  Register C (.D(multiplexer_1_out), .C(CLK), .en(U_C), .Q(C_o));
  Register V (.D(multiplexer_2_out), .C(CLK), .en(U_V), .Q(REG[6]));
  Multiplexer multiplexer_3 (.sel(WR), .in_0(Z_i), .in_1(BUS[1]), .out(multiplexer_3_out));
  Register I (.D(BUS[2]), .C(CLK), .en(U_I), .Q(I_o));
  Register Z (.D(multiplexer_3_out), .C(CLK), .en(U_Z), .Q(REG[1]));
  Multiplexer multiplexer_4 (.sel(WR), .in_0(N_i), .in_1(BUS[7]), .out(multiplexer_4_out));
  Register N (.D(multiplexer_4_out), .C(CLK), .en(U_N), .Q(N_o));
  Register D (.D(BUS[3]), .C(CLK), .en(U_D), .Q(D_o));
  assign BUS = OE ? {N_o, REG[6], 1'b1, REG[4], D_o, I_o, REG[1], C_o} : 8'bz;  // Driver driver_1
  not not_1 (REG[4], B_i);
  // Pins of 1 and 8 bits meet at {N_o, REG[6], 1'b1, REG[4], D_o, I_o, REG[1], C_o}

  assign {REG[7], REG[5], REG[3:2], REG[0]} = {N_o, 1'b1, D_o, I_o, C_o};
  assign V_o = REG[6];
  assign Z_o = REG[1];

  // Other names for the same wires on the sheet: B_o = REG[4]; C_B = BUS[0]; Z_B = BUS[1]; I_B = BUS[2]; D_B = BUS[3];
  //   V_B = BUS[6]; N_B = BUS[7]
endmodule
