// Digital circuit interrupt.dig as structural Verilog
module interrupt (
  input  I_in,
  input  N_in,
  input  R_in,
  input  I_flag,
  input  HLD,
  input  CLK,
  output INT,
  output NMI,
  output RST,
  output WAK
);

  wire and_1_out, and_2_out, and_3_out, and_4_out, delay_1_out, delay_2_out, INT_q, reset_1_out, rs_ff_as_1_q;

  Delay delay_1 (.in(N_in), .out(delay_1_out));
  Delay delay_2 (.in(HLD), .out(delay_2_out));
  and and_1 (and_1_out, N_in, ~delay_1_out);  // And
  and and_2 (and_2_out, HLD, ~delay_2_out);  // And
  RS_FF_AS rs_ff_as_1 (.S(and_1_out), .R(and_2_out), .Q(rs_ff_as_1_q));  // open: nQ
  and and_3 (and_3_out, CLK, ~HLD);  // And
  Reset #(.invertOutput("false")) reset_1 (.out(reset_1_out));
  Register u_INT (.D(I_in), .C(CLK), .en(~HLD), .Q(INT_q));
  Register u_NMI (.D(rs_ff_as_1_q), .C(CLK), .en(~HLD), .Q(NMI));
  D_FF_AS u_RST (.Set(reset_1_out), .D(R_in), .C(and_3_out), .Clr(1'b0), .Q(RST));  // open: nQ
  and and_4 (and_4_out, ~I_flag, INT_q);  // And
  or or_1 (INT, and_4_out, NMI, RST);
  or or_2 (WAK, INT_q, INT);

  // Other names for the same wires on the sheet: INT_HOLD = HLD
endmodule
