// Digital circuit constant.dig as structural Verilog
module constant (
  input  [2:0] IN,
  input  OE,
  output [7:0] BUS,
  output [7:0] REG
);

  or or_1 (REG[7], IN[1], IN[2]);
  assign BUS = OE ? {{5{REG[7]}}, IN} : 8'bz;  // Driver driver_1

  assign REG[6:0] = {{4{REG[7]}}, IN};
endmodule
