// Digital circuit cpu.dig as structural Verilog
module cpu (
  input  RST,
  input  NMI,
  input  INT,
  input  CLK,
  output [15:0] AD,
  output [7:0] DA,
  output WR
);

  wire ALU_c_o, ALU_v, Bus_Zero_eq, C_ALU, C_FLAG, Ci_ALU, CNT_SP, D_FLAG, DIR_SP, I_FLAG, INC_ADDRH,
       INC_ADDRL, INC_PC, INT_HOLD, INT_nmi, INT_rst, INT_wak, INTR, N_B, N_FLAG, OE_A, OE_ACC, OE_ADDRH,
       OE_ADDRL, OE_ALU, OE_B, OE_CONST, OE_FLAGS, OE_PCH, OE_PCL, OE_RAM, OE_SP, OE_X, OE_Y, OV_ADDRL,
       PCL_ov, RST_uSTEP, UPD_C, UPD_D, UPD_I, UPD_N, UPD_V, UPD_Z, V_FLAG, WR_A, WR_ACC, WR_ADDRH, WR_ADDRL,
       WR_B, WR_FLAGS, WR_INST, WR_PCH, WR_PCL, WR_SP, WR_X, WR_Y, Z_ALU, Z_FLAG;
  wire [1:0] SEL_ADDR;
  wire [3:0] CONST, SEL_FLAGIN;
  wire [6:0] B_reg;
  wire [7:0] A_reg, ACC_reg, ADDR_H, ADDR_L, ALU_y, CONST_reg, PC_H, PC_L, PCH_bus, PS_reg, SP, uCODE_d,
       X_reg, Y_reg;
  wire [12:0] uSTEP_out;

  counter PCH (.EN(PCL_ov), .DIR(1'b0), .WR(WR_PCH), .OE(OE_PCH), .CLK(CLK), .BUS(PCH_bus), .REG(PC_H));  // open: OV
  counter ADDRH (
    .EN(INC_ADDRH), .DIR(1'b0), .WR(WR_ADDRH), .OE(OE_ADDRH), .CLK(CLK), .BUS(PCH_bus), .REG(ADDR_H));  // open: OV
  // Probe on PC_H
  // Probe on ADDR_H
  Multiplexer #(.Selector_Bits(2), .Bits(16)) multiplexer_1 (
    .sel(SEL_ADDR), .in_0({PC_H, PC_L}), .in_1({ADDR_H, ADDR_L}), .in_2({{8{1'b0}}, ADDR_L}),
    .in_3({8'h1, SP}), .out(AD));
  // Probe on SEL_ADDR
  counter PCL (.EN(INC_PC), .DIR(1'b0), .WR(WR_PCL), .OE(OE_PCL), .CLK(CLK), .BUS(PCH_bus), .REG(PC_L), .OV(PCL_ov));
  counter ADDRL (
    .EN(INC_ADDRL), .DIR(1'b0), .WR(WR_ADDRL), .OE(OE_ADDRL), .CLK(CLK), .BUS(PCH_bus), .REG(ADDR_L),
    .OV(OV_ADDRL));
  counter u_SP (.EN(CNT_SP), .DIR(DIR_SP), .WR(WR_SP), .OE(OE_SP), .CLK(CLK), .BUS(PCH_bus), .REG(SP));  // open: OV
  assign PCH_bus = OE_RAM ? DA : 8'bz;  // Driver driver_1
  assign DA = WR ? PCH_bus : 8'bz;  // Driver driver_2
  // Probe on PC_L
  // Probe on ADDR_L
  // Probe on SP
  // Probe BUS on PCH_bus
  register ACC (.WR(WR_ACC), .OE(OE_ACC), .CLK(CLK), .BUS(PCH_bus), .REG(ACC_reg));
  register X (.WR(WR_X), .OE(OE_X), .CLK(CLK), .BUS(PCH_bus), .REG(X_reg));
  register Y (.WR(WR_Y), .OE(OE_Y), .CLK(CLK), .BUS(PCH_bus), .REG(Y_reg));
  Counter #(.Bits(4)) uSTEP (.en(1'b1), .C(CLK), .clr(RST_uSTEP), .out(uSTEP_out[3:0]));  // open: ovf
  Register #(.Bits(8)) INSTR (.D(PCH_bus), .C(CLK), .en(WR_INST), .Q(uSTEP_out[11:4]));
  interrupt u_INT (
    .I_in(INT), .N_in(NMI), .R_in(RST), .I_flag(I_FLAG), .HLD(INT_HOLD), .CLK(CLK), .INT(INTR),
    .NMI(INT_nmi), .RST(INT_rst), .WAK(INT_wak));
  // Probe on ACC_reg
  // Probe on X_reg
  // Probe on Y_reg
  // Probe on uSTEP_out[3:0]
  // Probe on uSTEP_out[11:4]
  register A (.WR(WR_A), .OE(OE_A), .CLK(CLK), .BUS(PCH_bus), .REG(A_reg));
  register B (.WR(WR_B), .OE(OE_B), .CLK(CLK), .BUS(PCH_bus), .REG({N_B, B_reg}));
  constant u_CONST (.IN(CONST), .OE(OE_CONST), .BUS(PCH_bus), .REG(CONST_reg));
  Multiplexer #(.Selector_Bits(4)) multiplexer_2 (
    .sel(SEL_FLAGIN), .in_0(C_FLAG), .in_1(Z_FLAG), .in_2(V_FLAG), .in_3(N_FLAG), .in_4(C_ALU), .in_5(N_B),
    .in_6(INTR), .in_7(INT_nmi), .in_8(INT_rst), .in_9(INT_wak), .in_10(OV_ADDRL), .in_11(Z_ALU),
    .in_12(1'b0), .in_13(1'b0), .in_14(1'b0), .in_15(1'b0), .out(uSTEP_out[12]));
  // Probe on CONST
  // Probe on SEL_FLAGIN
  // Probe on A_reg
  // Probe on {N_B, B_reg}
  // Probe on CONST_reg
  // Probe on uSTEP_out
  ROM #(.AddrBits(13), .Bits(32), .generic("if(args.cpuModel = 0) { this.Label = \"6502\"; this.lastDataFile = \"ucode_6502.hex\"; } else { this.Label = \"65C02\"; this.lastDataFile = \"ucode_65c02.hex\"; }")) uCODE (
    .A(uSTEP_out), .sel(1'b1),
    .D({INT_HOLD, DIR_SP, CNT_SP, INC_ADDRH, INC_ADDRL, UPD_N, UPD_V, UPD_D, UPD_I, UPD_Z, UPD_C, RST_uSTEP, INC_PC, Ci_ALU, SEL_ADDR, SEL_FLAGIN, CONST, uCODE_d}));
  alu ALU (
    .A(A_reg), .B({N_B, B_reg}), .C_i(Ci_ALU), .D_i(D_FLAG), .Op(CONST), .OE(OE_ALU), .BUS(PCH_bus),
    .Y(ALU_y), .C_o(ALU_c_o), .V(ALU_v));
  // Probe on CONST
  // Probe on {INT_HOLD, DIR_SP, CNT_SP, INC_ADDRH, INC_ADDRL, UPD_N, UPD_V, UPD_D, UPD_I, UPD_Z, UPD_C, RST_uSTEP, INC_PC, Ci_ALU, SEL_ADDR, SEL_FLAGIN, CONST, uCODE_d}
  // Probe on ALU_y
  Comparator #(.Bits(8)) Bus_Zero (.a(PCH_bus), .b({8{1'b0}}), .eq(Bus_Zero_eq));  // open: gt, lt
  Register ALU_Carry (.D(ALU_c_o), .C(CLK), .en(OE_ALU), .Q(C_ALU));
  Register ALU_Zero (.D(Bus_Zero_eq), .C(CLK), .en(OE_ALU), .Q(Z_ALU));
  Decoder #(.Selector_Bits(4)) decoder_1 (
    .sel(uCODE_d[7:4]), .out_1(WR_PCL), .out_2(WR_PCH), .out_3(WR_ADDRL), .out_4(WR_ADDRH), .out_5(WR),
    .out_6(WR_ACC), .out_7(WR_X), .out_8(WR_Y), .out_9(WR_SP), .out_10(WR_A), .out_11(WR_B),
    .out_12(WR_FLAGS), .out_13(WR_INST));  // open: out_0, out_14, out_15
  // Probe on uCODE_d[7:4]
  flags PS (
    .WR(WR_FLAGS), .C_i(ALU_c_o), .Z_i(Bus_Zero_eq), .B_i(INTR), .V_i(ALU_v), .U_C(UPD_C), .U_Z(UPD_Z),
    .U_I(UPD_I), .U_D(UPD_D), .U_V(UPD_V), .U_N(UPD_N), .OE(OE_FLAGS), .CLK(CLK), .BUS(PCH_bus),
    .C_o(C_FLAG), .Z_o(Z_FLAG), .I_o(I_FLAG), .D_o(D_FLAG), .V_o(V_FLAG), .N_o(N_FLAG), .REG(PS_reg));
  // Probe on uCODE_d[3:0]
  Decoder #(.Selector_Bits(4)) decoder_2 (
    .sel(uCODE_d[3:0]), .out_1(OE_PCL), .out_2(OE_PCH), .out_3(OE_ADDRL), .out_4(OE_ADDRH), .out_5(OE_RAM),
    .out_6(OE_ACC), .out_7(OE_X), .out_8(OE_Y), .out_9(OE_SP), .out_10(OE_A), .out_11(OE_B),
    .out_12(OE_FLAGS), .out_13(OE_ALU), .out_14(OE_CONST));  // open: out_0, out_15
  // Probe on PS_reg

  // Other names for the same wires on the sheet: OP_ALU[3:0] = CONST; WR_RAM = WR

  // Notes on the sheet:
  //   CLK: Hz: 2147483647
endmodule

/* Code that sets the parameters or builds the circuit:
cpuModel := 0;
*/
