// Digital circuit interrupt.dig as structural Verilog
module interrupt (
  input  I_in,
  input  N_in,
  input  R_in,
  input  I_flag,
  input  HLD,
  input  CLK,
  output INT,
  output NMI,
  output RST
);

  wire and_1_out, and_2_out, INT_q, reset_1_out;

  and and_1 (and_1_out, CLK, ~HLD);  // And
  Reset #(.invertOutput("false")) reset_1 (.out(reset_1_out));
  Register u_INT (.D(I_in), .C(CLK), .en(~HLD), .Q(INT_q));
  Register u_NMI (.D(N_in), .C(CLK), .en(~HLD), .Q(NMI));
  D_FF_AS u_RST (.Set(reset_1_out), .D(R_in), .C(and_1_out), .Clr(1'b0), .Q(RST));  // open: nQ
  and and_2 (and_2_out, ~I_flag, INT_q);  // And
  or or_1 (INT, and_2_out, NMI, RST);

  // Other names for the same wires on the sheet: INT_HOLD = HLD
endmodule
