// Digital circuit register.dig as structural Verilog
module register (
  input  WR,
  input  OE,
  input  CLK,
  output [7:0] BUS,
  output [7:0] REG
);

  Register #(.Bits(8)) register_1 (.D(BUS), .C(CLK), .en(WR), .Q(REG));
  assign BUS = OE ? REG : 8'bz;  // Driver driver_1
endmodule
